# Fritzing sketch finalProject_sensors_diagram (saved by Fritzing 0.9.3b)
perfboards: 1
breadboards: 1

parts:
  R1 = Resistor [resistance=10k tolerance=±5% package=THT]
  J2 = Basic Force Sensing Resistor (FSR) [package=THT]
  J2_2 = Basic Force Sensing Resistor (FSR) [package=THT]
  Arduino1 = Arduino Uno (Rev3)
  R1_2 = Resistor [tolerance=±5% resistance=10k package=THT]
  J3 = Infrared Proximity Sensor

nets:
  N1: R1.Pin_0, J2.pin_1, Arduino1.A1
  N2: R1.Pin_1, Arduino1.GND, R1_2.Pin_1
  N3: J2.pin_0, J2_2.pin_0, Arduino1.5V
  N4: J2_2.pin_1, Arduino1.A0, R1_2.Pin_0
  N5: Arduino1.A2, J3.Vout

notes:
  Pretend this is a joystick
